// Logisim project processor.circ as structural Verilog: 10 circuits, main circuit IFstage
module IFstage (
  input  [31:0] in_1,
  input  in_2,
  input  in_3,
  input  in_4,
  input  in_5,
  output [31:0] out_6,
  output [31:0] out_7
);

  wire not_1_out;
  wire [31:0] multiplexer_1_out, PC_q, ram_1_dout;

  Register #(.width(32)) PC (.D(multiplexer_1_out), .en(not_1_out), .clk(in_4), .Q(PC_q), .clr(in_5));
  not not_1 (not_1_out, in_3);
  Multiplexer #(.width(32), .enable("false")) multiplexer_1 (
    .in0(in_1), .in1(out_6), .out(multiplexer_1_out));  // open: sel
  Adder #(.width(32)) adder_1 (.a(32'h4), .b(PC_q), .out(out_6));  // open: cin, cout
  RAM #(.addrWidth(24), .dataWidth(32), .databus("bibus")) ram_1 (
    .addr(PC_q[25:2]), .dout(ram_1_dout));  // open: we, oe, clk, din
  Multiplexer #(.width(32), .enable("false")) multiplexer_2 (
    .in0({32{1'b0}}), .in1(ram_1_dout), .out(out_7), .sel(in_2));
endmodule

module IFIDpipe (
  input  in_1,
  input  [31:0] in_2,
  input  [31:0] in_3,
  input  in_4,
  input  in_5,
  output [31:0] out_6,
  output [31:0] out_7
);

  Register #(.width(32)) register_1 (.D(in_2), .en(in_1), .clk(in_4), .Q(out_6), .clr(in_5));
  Register #(.width(32)) register_2 (.D(in_3), .en(in_1), .clk(in_4), .Q(out_7), .clr(in_5));
endmodule

module IDstage (
  input  [31:0] in_1,
  input  [31:0] in_2,
  input  stall,
  output [31:0] out_4,
  output out_5,
  output [31:0] out_6,
  output [31:0] out_7,
  output [31:0] out_8,
  output [2:0] out_9,
  output out_10,
  output [1:0] out_11,
  output [1:0] out_12,
  output out_13,
  output out_14,
  output out_15,
  output out_16,
  output [4:0] out_17,
  output out_18,
  output [31:0] out_19
);

  wire comparator_1_eq, decoder_1_out0, decoder_1_out1, decoder_1_out2, decoder_1_out8, decoder_1_out9,
       decoder_1_out11, not_1_out;
  wire [27:0] bit_extender_1_out, shifter_1_out;
  wire [31:0] adder_1_out, bit_extender_2_out, bit_extender_3_out, multiplexer_4_out, multiplexer_5_out,
       shifter_2_out;

  assign bit_extender_1_out = {{2{1'b0}}, in_2[25:0]};  // Bit_Extender bit_extender_1
  Shifter #(.width(28)) shifter_1 (.in(bit_extender_1_out), .\dist (5'b00010), .out(shifter_1_out));
  Decoder #(.select(4)) decoder_1 (
    .out0(decoder_1_out0), .out1(decoder_1_out1), .out2(decoder_1_out2), .out3(out_13),
    .out8(decoder_1_out8), .out9(decoder_1_out9), .out10(out_16), .out11(decoder_1_out11), .out12(out_9[0]),
    .out13(out_9[1]), .out14(out_9[2]), .out15(out_10));  // open: out4, out5, out6, out7, sel, en
  assign bit_extender_2_out = {{16{in_2[15]}}, in_2[15:0]};  // Bit_Extender bit_extender_2
  assign bit_extender_3_out = {{16{in_2[15]}}, in_2[15:0]};  // Bit_Extender bit_extender_3
  Multiplexer #(.width(5), .enable("false")) multiplexer_1 (
    .in0(in_2[20:16]), .in1(in_2[15:11]), .sel(decoder_1_out11));  // open: out
  Shifter #(.width(32)) shifter_2 (.in(bit_extender_2_out), .\dist (5'b00010), .out(shifter_2_out));
  Multiplexer #(.width(32), .enable("false")) multiplexer_2 (
    .in0(bit_extender_2_out), .in1(bit_extender_3_out), .out(out_8), .sel(decoder_1_out2));
  Adder #(.width(32)) adder_1 (.a(in_1), .b(shifter_2_out), .out(adder_1_out));  // open: cin, cout
  Multiplexer #(.width(32), .enable("false")) multiplexer_3 (
    .in0({in_1[31:28], shifter_1_out}), .in1(adder_1_out), .out(out_4), .sel(decoder_1_out1));
  Multiplexer #(.width(32), .enable("false")) multiplexer_4 (.in1(out_19), .out(multiplexer_4_out));  // open: in0, sel
  Multiplexer #(.width(32), .enable("false")) multiplexer_5 (.in1(out_19), .out(multiplexer_5_out));  // open: in0, sel
  Comparator #(.width(32)) comparator_1 (
    .a(multiplexer_4_out), .b(multiplexer_5_out), .eq(comparator_1_eq));  // open: gt, lt
  and and_1 (out_5, comparator_1_eq, decoder_1_out0);
  not not_1 (not_1_out, stall);
  and and_2 (out_15, decoder_1_out8, not_1_out);
  and and_3 (out_18, decoder_1_out9, not_1_out);
endmodule

module IDEXpipe (
  input  in_1,
  input  [31:0] in_2,
  input  [31:0] in_3,
  input  [31:0] in_4,
  input  [2:0] in_5,
  input  in_6,
  input  [1:0] in_7,
  input  [1:0] in_8,
  input  in_9,
  input  in_10,
  input  in_11,
  input  in_12,
  input  [4:0] in_13,
  input  in_14,
  input  in_15,
  output [31:0] out_16,
  output [31:0] out_17,
  output [31:0] out_18,
  output [2:0] out_19,
  output out_20,
  output [1:0] out_21,
  output [1:0] out_22,
  output out_23,
  output out_24,
  output out_25,
  output out_26,
  output [4:0] out_27,
  output out_28
);

  Register #(.width(32)) rdA (.D(in_2), .en(1'b1), .clk(in_1), .Q(out_16), .clr(in_15));
  Register #(.width(32)) rdB (.D(in_3), .en(1'b1), .clk(in_1), .Q(out_17), .clr(in_15));
  Register #(.width(32)) imm (.D(in_4), .en(1'b1), .clk(in_1), .Q(out_18), .clr(in_15));
  Register #(.width(3)) alucont (.D(in_5), .en(1'b1), .clk(in_1), .Q(out_19), .clr(in_15));
  Register #(.width(1)) aluSrc (.D(in_6), .en(1'b1), .clk(in_1), .Q(out_20), .clr(in_15));
  Register #(.width(2)) forwardA (.D(in_7), .en(1'b1), .clk(in_1), .Q(out_21), .clr(in_15));
  Register #(.width(2)) forwardB (.D(in_8), .en(1'b1), .clk(in_1), .Q(out_22), .clr(in_15));
  Register #(.width(1)) isLoad (.D(in_9), .en(1'b1), .clk(in_1), .Q(out_23), .clr(in_15));
  Register #(.width(1)) ldstBypass (.D(in_10), .en(1'b1), .clk(in_1), .Q(out_24), .clr(in_15));
  Register #(.width(1)) memWrite (.D(in_11), .en(1'b1), .clk(in_1), .Q(out_25), .clr(in_15));
  Register #(.width(1)) memToReg (.D(in_12), .clk(in_1), .Q(out_26), .clr(in_15));  // open: en
  Register #(.width(5)) rd (.D(in_13), .en(1'b1), .clk(in_1), .Q(out_27), .clr(in_15));
  Register #(.width(1)) regWrite (.D(in_14), .en(1'b1), .clk(in_1), .Q(out_28), .clr(in_15));
endmodule

module ALU (
  input  [31:0] in_1,
  input  [31:0] in_2,
  input  [2:0] in_3,
  output [31:0] out_4
);

  wire [31:0] adder_1_out, and_1_out, bit_extender_1_out, multiplexer_1_out, or_1_out, xor_1_out;

  assign bit_extender_1_out = {{31{in_3[0]}}, in_3[0]};  // Bit_Extender bit_extender_1
  Adder #(.width(32)) adder_1 (.a(in_1), .b(xor_1_out), .out(adder_1_out));  // open: cin, cout
  assign xor_1_out = in_2 ^ bit_extender_1_out;  // XOR_Gate xor_1, 32 bits wide
  assign and_1_out = in_1 & in_2;  // AND_Gate and_1, 32 bits wide
  assign or_1_out = in_1 | in_2;  // OR_Gate or_1, 32 bits wide
  Multiplexer #(.width(32), .enable("false")) multiplexer_1 (
    .in0(and_1_out), .in1(or_1_out), .out(multiplexer_1_out), .sel(in_3[0]));
  Multiplexer #(.width(32), .enable("false")) multiplexer_2 (
    .in0(multiplexer_1_out), .in1(adder_1_out), .out(out_4), .sel(in_3[1]));
endmodule

module EXstage (
  input  [31:0] in_1,
  input  [31:0] in_2,
  input  [31:0] in_3,
  input  [2:0] in_4,
  input  in_5,
  input  [1:0] in_6,
  input  [1:0] in_7,
  input  in_8,
  input  in_9,
  input  in_10,
  input  in_11,
  input  [4:0] in_12,
  input  in_13,
  input  [31:0] in_14,
  input  [31:0] in_15,
  output [31:0] out_16,
  output [31:0] out_17,
  output out_18,
  output out_19,
  output out_20,
  output out_21,
  output [4:0] out_22,
  output out_23
);

  wire [31:0] multiplexer_1_out, multiplexer_3_out;

  Multiplexer #(.select(2), .width(32), .enable("false")) multiplexer_1 (
    .in0(in_1), .in1(in_14), .in2(in_15), .out(multiplexer_1_out), .sel(in_6));  // open: in3
  Multiplexer #(.select(2), .width(32), .enable("false")) multiplexer_2 (
    .in0(in_2), .in1(in_14), .in2(in_15), .out(out_17), .sel(in_7));  // open: in3
  Multiplexer #(.width(32), .enable("false")) multiplexer_3 (
    .in0(out_17), .in1(in_3), .out(multiplexer_3_out), .sel(in_5));
  ALU alu_1 (.in_3(in_4), .in_1(multiplexer_1_out), .in_2(multiplexer_3_out), .out_4(out_16));

  assign out_18 = in_8;
  assign out_19 = in_9;
  assign out_20 = in_10;
  assign out_21 = in_11;
  assign out_22 = in_12;
  assign out_23 = in_13;
endmodule

module EXMEMpipe (
  input  in_1,
  input  [31:0] in_2,
  input  [31:0] in_3,
  input  in_4,
  input  in_5,
  input  in_6,
  input  in_7,
  input  [4:0] in_8,
  input  in_9,
  input  in_10,
  output [31:0] out_11,
  output [31:0] out_12,
  output out_13,
  output out_14,
  output out_15,
  output out_16,
  output [4:0] out_17,
  output out_18
);

  Register #(.width(32)) register_1 (.D(in_2), .en(1'b1), .clk(in_1), .Q(out_11), .clr(in_10));
  Register #(.width(32)) register_2 (.D(in_3), .en(1'b1), .clk(in_1), .Q(out_12), .clr(in_10));
  Register #(.width(1)) register_3 (.D(in_4), .en(1'b1), .clk(in_1), .Q(out_13), .clr(in_10));
  Register #(.width(1)) register_4 (.D(in_5), .en(1'b1), .clk(in_1), .Q(out_14), .clr(in_10));
  Register #(.width(1)) register_5 (.D(in_6), .en(1'b1), .clk(in_1), .Q(out_15), .clr(in_10));
  Register #(.width(1)) register_6 (.D(in_7), .en(1'b1), .clk(in_1), .Q(out_16), .clr(in_10));
  Register #(.width(5)) register_7 (.D(in_8), .en(1'b1), .clk(in_1), .Q(out_17), .clr(in_10));
  Register #(.width(1)) register_8 (.D(in_9), .en(1'b1), .clk(in_1), .Q(out_18), .clr(in_10));
endmodule

module MEMstage (
  input  [31:0] in_1,
  input  [31:0] in_2,
  input  in_3,
  input  in_4,
  input  in_5,
  input  in_6,
  input  [4:0] in_7,
  input  in_8,
  input  [31:0] in_9,
  output [31:0] out_10,
  output [31:0] out_11,
  output out_12,
  output [4:0] out_13,
  output out_14,
  output out_15,
  output [4:0] out_16,
  output out_17
);

  wire [31:0] multiplexer_1_out;

  Multiplexer #(.width(32), .enable("false")) multiplexer_1 (
    .in0(in_2), .in1(in_9), .out(multiplexer_1_out), .sel(in_4));
  RAM #(.addrWidth(5), .dataWidth(32), .databus("bibus")) ram_1 (
    .addr(in_1[6:2]), .we(in_5), .din(multiplexer_1_out), .dout(out_11));  // open: oe, clk

  assign out_10 = in_1;
  assign out_12 = in_6;
  assign out_13 = in_7;
  assign out_14 = in_8;
  assign out_15 = in_3;
  assign out_16 = in_7;
  assign out_17 = in_8;
endmodule

module MEMWBpipe (
  input  in_1,
  input  [31:0] in_2,
  input  [31:0] in_3,
  input  in_4,
  input  [4:0] in_5,
  input  in_6,
  input  in_7,
  output [31:0] out_8,
  output [31:0] out_9,
  output out_10,
  output [4:0] out_11,
  output out_12
);

  Register #(.width(32)) register_1 (.D(in_2), .en(1'b1), .clk(in_1), .Q(out_8), .clr(in_7));
  Register #(.width(32)) register_2 (.D(in_3), .en(1'b1), .clk(in_1), .Q(out_9), .clr(in_7));
  Register #(.width(1)) register_3 (.D(in_4), .en(1'b1), .clk(in_1), .Q(out_10), .clr(in_7));
  Register #(.width(5)) register_4 (.D(in_5), .en(1'b1), .clk(in_1), .Q(out_11), .clr(in_7));
  Register #(.width(1)) register_5 (.D(in_6), .en(1'b1), .clk(in_1), .Q(out_12), .clr(in_7));
endmodule

module WBstage (
  input  [31:0] in_1,
  input  [31:0] in_2,
  input  in_3,
  input  [4:0] in_4,
  input  in_5,
  output [31:0] out_6,
  output [4:0] out_7,
  output out_8
);

  Multiplexer #(.width(32), .enable("false")) multiplexer_1 (.in0(in_1), .in1(in_2), .out(out_6), .sel(in_3));

  assign out_7 = in_4;
  assign out_8 = in_5;
endmodule
